// Digital circuit alu.dig as structural Verilog
module alu (
  input  [7:0] A,
  input  [7:0] B,
  input  [3:0] Op,
  output [7:0] Res,
  output Cout,
  output Equal
);

  wire [7:0] R_AminB, R_AplusB, R_BminA, R_MinA, R_MinB, R_RotateLeftA, R_RotateRight_A, R_ShiftLeftA,
       R_ShiftRightA;

  add8b add8b_1 (.A(A), .B(B), .Cin(1'b0), .X(R_AplusB));  // open: Cout
  min8b min8b_1 (.A(A), .B(B), .Cin(1'b0), .X(R_AminB));  // open: Cout
  min8b min8b_2 (.A(B), .B(A), .Cin(1'b0), .X(R_BminA));  // open: Cout
  _2c _2c_1 (.A(A), .X(R_MinA));
  _2c _2c_2 (.A(B), .X(R_MinB));
  sl8b sl8b_1 (.A(A), .S(B), .X(R_ShiftLeftA));
  sr8b sr8b_1 (.A(A), .S(B), .X(R_ShiftRightA));
  rl8b rl8b_1 (.A(A), .S(B), .X(R_RotateLeftA));
  rr8b rr8b_1 (.A(A), .S(B), .X(R_RotateRight_A));
  equal equal_1 (.A(A), .B(B), .Equal(Equal));
  Multiplexer #(.Selector_Bits(4), .Bits(8)) multiplexer_1 (
    .sel(Op), .in_0(R_AplusB), .in_1(R_AminB), .in_2(R_BminA), .in_3({8{1'b0}}), .in_4(A), .in_5(B),
    .in_6(R_MinA), .in_7(R_MinB), .in_8(R_ShiftLeftA), .in_9(R_ShiftRightA), .in_10(R_RotateLeftA),
    .in_11(R_RotateRight_A), .in_12({8{1'b0}}), .in_13({8{1'b0}}), .in_14({8{1'b0}}), .in_15({8{1'b1}}),
    .out(Res));
  BitSelector #(.Selector_Bits(3)) bitselector_1 (.in(Res), .sel(3'b111), .out(Cout));

  // Other names for the same wires on the sheet: R_OnlyA[7:0] = A; R_OnlyB[7:0] = B
endmodule
